// Logisim project Exercicio1Casa.circ as structural Verilog: 1 circuit, main circuit main
module main (
  input  in_1,
  input  in_2,
  input  in_3,
  input  in_4,
  input  in_5
);

  wire and_1_out, and_2_out, or_1_out;

  and and_1 (and_1_out, in_1, in_2, in_3);
  and and_2 (and_2_out, in_4, in_5);
  or or_1 (or_1_out, and_1_out, and_2_out);
  LED led_1 (.in(or_1_out));
endmodule
