// Logisim project Exercicio2Casa.circ as structural Verilog: 1 circuit, main circuit main
module main (
  input  A,
  input  B,
  input  C,
  input  D,
  input  E,
  input  F
);

  wire S1_out, S2_out, S3_out, S_out;

  and S1 (S1_out, A, B);
  and S2 (S2_out, C, D);
  and S3 (S3_out, E, F);
  or S (S_out, S1_out, S2_out, S3_out);
  LED led_1 (.in(S_out));
endmodule
