// Logisim project Exercício2Lista2.circ as structural Verilog: 1 circuit, main circuit main
module main (
  input  A,
  input  C,
  input  B,
  input  D,
  input  E,
  input  F
);

  wire S1_out, S2_out, S3_out, S_out;

  and S1 (S1_out, A, C);
  or S2 (S2_out, B, D);
  and S3 (S3_out, E, F);
  LED led_1 (.in(S_out));
  or S (S_out, S1_out, S2_out, S3_out);
endmodule
