// Logisim project Exercício3Casa.circ as structural Verilog: 1 circuit, main circuit main
module main (
  input  A,
  input  B,
  input  C,
  input  D,
  input  A_2,
  input  B_2,
  input  C_2,
  input  D_2,
  input  A_3,
  input  B_3,
  input  C_3,
  input  D_3
);

  wire not_1_out, not_2_out, not_3_out, not_4_out, not_5_out, not_6_out, or_1_out, S1_out, S2_out, S3_out;

  not not_1 (not_1_out, D_2);
  not not_2 (not_2_out, A);
  and S1 (S1_out, not_2_out, B, not_3_out, D);
  not not_3 (not_3_out, C);
  not not_4 (not_4_out, B_2);
  and S2 (S2_out, A_2, not_4_out, not_5_out, not_1_out);
  not not_5 (not_5_out, C_2);
  not not_6 (not_6_out, B_3);
  and S3 (S3_out, A_3, not_6_out, C_3, D_3);
  LED S (.in(or_1_out));
  or or_1 (or_1_out, S1_out, S2_out, S3_out);
endmodule
