// Logisim project Exercício3Lista2.circ as structural Verilog: 1 circuit, main circuit main
module main (
  input  A,
  input  B,
  input  C,
  input  D,
  input  A_2,
  input  B_2,
  input  C_2,
  input  D_2,
  input  A_3,
  input  B_3,
  input  C_3,
  input  D_3
);

  wire and_1_out, and_2_out, and_3_out, not_1_out, not_2_out, not_3_out, not_4_out, not_5_out, not_6_out;

  not not_1 (not_1_out, C_2);
  not not_2 (not_2_out, A);
  not not_3 (not_3_out, B);
  and and_1 (and_1_out, not_2_out, not_3_out, C, D);
  and and_2 (and_2_out, A_2, not_4_out, not_1_out, not_5_out);
  not not_4 (not_4_out, B_2);
  not not_5 (not_5_out, D_2);
  not not_6 (not_6_out, B_3);
  and and_3 (and_3_out, A_3, not_6_out, C_3, D_3);
  // OR_Gate or_1 has open pins: in1=and_1_out, in2=and_2_out, in4=and_3_out, out=open

  // Notes on the sheet:
  //   Expressão Boleana = (!A !B C D) + (A !B !C !D) + (A !B C D)
endmodule
